# Fritzing sketch relogio-rua (saved by Fritzing 0.9.10b)

parts:
  U1 = ESP32-38PinWide [part_number=ESP32-38PinWide]
  DHT1 = DHT22 Humidity and Temperature Sensor
  OLED_I2C1 = OLED 128x64 I2C Monochrome Display

nets:
  GND: U1.GPIO11, DHT1.GND, OLED_I2C1.GND
  VDD: U1.VIN, DHT1.VDD, OLED_I2C1.VDD
  N1: U1.GPIO21, OLED_I2C1.SDA
  N2: U1.GPIO22, OLED_I2C1.SCK
  N3: U1.GPIO23, DHT1.DATA

notes:
  Micrcontrolador
  Display OLED
  Temperatura
  Umidade

custom parts:
  ESP32-38PinWide: Generic 38-Pin ESP32 with wide format (only access to one side of pins on a breadboard) based on Stephen Lilley's HiLetgo ESP-WROOM-32 ESP32 ESP-32S Development Board.
